# Fritzing sketch CDLE (saved by Fritzing 0.9.3b)
stripboards: 3

parts:
  J1 = Terminal Block - 3 pins [package=THT]
  J3 = Terminal Block - 3 pins [package=THT]
  J5 = Terminal Block - 3 pins [package=THT]
  Part1 = Adafruit T-Cobbler Plus [part_number="Adafruit #1989 and #2028"]
  J2 = Terminal Block - 3 pins [package=THT]
  J4 = Terminal Block - 3 pins [package=THT]
  IC1 = MCP3008 8-channel 10-bit ADC [part_number=MCP3008]

nets:
  N1: J1.Line_2, Part1.+3.3V, J2.Line_1, J4.Line_2
  N2: J1.Line_3, J3.Line_3, J5.Line_1, Part1.GND, J4.Line_1, J4.Line_3, IC1.no_name_yet#9, IC1.no_name_yet#14
  N3: J3.Line_1, Part1.SCL
  N4: J3.Line_2, Part1.SDA
  N5: J5.Line_2, Part1.+3.3V_2, IC1.no_name_yet#15, IC1.no_name_yet#16
  N6: J5.Line_3, IC1.no_name_yet#2
  N7: Part1.MOSI, IC1.no_name_yet#11
  N8: Part1.MISO, IC1.no_name_yet#12
  N9: Part1.SCLK, IC1.no_name_yet#13
  N10: Part1.GPIO13, J2.Line_2
  N11: Part1.CE0, IC1.no_name_yet#10
  N12: Part1.GPIO12, J2.Line_3

custom parts:
  Terminal Block - 3 pins: Generic Screw Terminal 9.5mm
  Adafruit T-Cobbler Plus: The Raspberry Pi has landed on the Maker World like a 40-GPIO pinned, quad-USB ported, credit card sized bomb of DIY joy. And while you can use most of our great Model B accessories by hooking up our downgrade cable, its probably a good time to upgrade your set up and accessorize using all of the 40 pins. That's why we now carry the Assembled Adafruit Pi T-Cobbler Plus - Breakout + Cable for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
